// Logisim project e2521581.circ as structural Verilog: 1 circuit, main circuit main
module main (
  input  A1,
  input  A0,
  input  B1,
  input  B0,
  input  O2,
  input  O1,
  input  O0,
  input  in_8,
  output S,
  output L0,
  output L1,
  output L2,
  output L3,
  output L4,
  output L5,
  output L6
);

  wire and_1_out, and_2_out, and_3_out, and_4_out, and_5_out, and_6_out, and_7_out, and_8_out, and_9_out,
       and_10_out, n4_to_1_mux_x2_74153_1_p6, n4_to_1_mux_x2_74153_2_p10, n4_to_1_mux_x2_74153_2_p11,
       n4_to_1_mux_x2_74153_3_p16, n4_to_1_mux_x2_74153_4_p10, n4_to_1_mux_x2_74153_5_p12,
       n4_to_1_mux_x2_74153_6_p14, nor_1_out, nor_2_out, not_1_out, not_2_out, not_3_out, not_4_out,
       not_5_out, or_1_out, or_2_out, or_3_out, or_4_out, or_5_out, or_6_out, xor_1_out, xor_2_out,
       xor_3_out, xor_4_out, xor_5_out, xor_6_out, xor_7_out, xor_8_out, xor_9_out;

  not not_1 (not_1_out, B0);
  and and_1 (and_1_out, not_1_out, A0);
  xor xor_1 (xor_1_out, A0, not_1_out);
  or or_1 (or_1_out, B0, B1);
  and and_2 (and_2_out, B1, B0);
  not not_2 (not_2_out, B1);
  and and_3 (and_3_out, not_2_out, A1);
  xor xor_2 (xor_2_out, A1, not_2_out);
  not not_3 (not_3_out, xor_1_out);
  and and_4 (and_4_out, B1, A1);
  and and_5 (and_5_out, B0, A0);
  xor xor_3 (xor_3_out, A0, B0);
  nor nor_1 (nor_1_out, A1, B1);
  nor nor_2 (nor_2_out, A0, B0);
  and and_6 (and_6_out, A1, B1);
  and and_7 (and_7_out, A0, B0);
  xor xor_4 (xor_4_out, A1, B1);
  xor xor_5 (xor_5_out, A0, B0);
  // _4_to_1_MUX__x2___74153 #(.Facing("east")) 4_to_1_mux_x2_74153_1: pin names not known; wires that end beside it: in_8, or_1_out, B1, and_2_out, 1'b0, n4_to_1_mux_x2_74153_1_p6
  // _4_to_1_MUX__x2___74153 #(.Facing("east")) 4_to_1_mux_x2_74153_2: pin names not known; wires that end beside it: B0, 1'b0, 1'b0, 1'b0, B1, B0, A0, A1, 1'b0, n4_to_1_mux_x2_74153_2_p10, n4_to_1_mux_x2_74153_2_p11
  // _4_to_1_MUX__x2___74153 #(.Facing("east")) 4_to_1_mux_x2_74153_3: pin names not known; wires that end beside it: 1'b0, 1'b0, 1'b0, B1, B0, 1'b0, 1'b0, 1'b0, 1'b0, 1'b0, A0, A0, A1, 1'b0, A1, n4_to_1_mux_x2_74153_3_p16
  or or_2 (or_2_out, and_3_out, and_8_out);
  and and_8 (and_8_out, xor_2_out, and_1_out);
  xor xor_6 (xor_6_out, and_1_out, xor_2_out);
  not not_4 (not_4_out, xor_6_out);
  and and_9 (and_9_out, or_2_out, not_3_out);
  or or_3 (or_3_out, and_4_out, and_10_out);
  xor xor_7 (xor_7_out, A1, B1);
  and and_10 (and_10_out, xor_7_out, and_5_out);
  xor xor_8 (xor_8_out, and_5_out, xor_7_out);
  xor xor_9 (xor_9_out, not_4_out, and_9_out);
  not not_5 (not_5_out, O2);
  // _4_to_1_MUX__x2___74153 #(.Facing("east")) 4_to_1_mux_x2_74153_4: pin names not known; wires that end beside it: xor_3_out, not_3_out, n4_to_1_mux_x2_74153_2_p10, n4_to_1_mux_x2_74153_1_p6, xor_5_out, and_7_out, nor_2_out, O2, not_5_out, n4_to_1_mux_x2_74153_4_p10
  // _4_to_1_MUX__x2___74153 #(.Facing("east")) 4_to_1_mux_x2_74153_5: pin names not known; wires that end beside it: xor_8_out, xor_9_out, n4_to_1_mux_x2_74153_2_p11, 1'b0, xor_4_out, and_6_out, nor_1_out, O0, O2, O1, not_5_out, n4_to_1_mux_x2_74153_5_p12
  // _4_to_1_MUX__x2___74153 #(.Facing("east")) 4_to_1_mux_x2_74153_6: pin names not known; wires that end beside it: or_3_out, 1'b0, n4_to_1_mux_x2_74153_3_p16, 1'b0, 1'b0, 1'b0, 1'b0, O0, O2, O0, O1, not_5_out, O1, n4_to_1_mux_x2_74153_6_p14
  // _3_to_8_decoder__74138 #(.Facing("east")) 3_to_8_decoder_74138_1: pin names not known; wires that end beside it: O0, O1, O2, or_2_out, 1'b0
  buf or_4 (or_4_out, n4_to_1_mux_x2_74153_4_p10);  // OR_Gate
  buf or_5 (or_5_out, n4_to_1_mux_x2_74153_5_p12);  // OR_Gate
  buf or_6 (or_6_out, n4_to_1_mux_x2_74153_6_p14);  // OR_Gate
  // NOT_Gate not_6 has open pins: in=open, out=S
  // _3_to_8_decoder__74138 #(.Facing("east")) 3_to_8_decoder_74138_2: pin names not known; wires that end beside it: or_4_out, or_5_out, or_6_out, 1'b1, 1'b0, L1, L3, L4, L5
  // NOT_Gate not_7 has open pins: in=open, out=L0
  // NOT_Gate not_8 has open pins: in=open, out=L1
  // NOT_Gate not_9 has open pins: in=open, out=L2
  // NOT_Gate not_10 has open pins: in=open, out=L3
  // NOT_Gate not_11 has open pins: in=open, out=L4
  // NOT_Gate not_12 has open pins: in=open, out=L5
  // NOT_Gate not_13 has open pins: in=open, out=L6
endmodule
