// Logisim project hw2-lab.circ as structural Verilog: 1 circuit, main circuit main
module main (
  input  B0,
  input  B1,
  input  A0,
  input  A1,
  input  O2,
  input  O1,
  output L0,
  output L1,
  output L2,
  output L3
);

  wire and_1_out, n4_to_1_mux_x2_74153_1_p8, n4_to_1_mux_x2_74153_1_p9, n4_to_1_mux_x2_74153_2_p12,
       n4_to_1_mux_x2_74153_2_p13, nor_1_out, nor_2_out, xor_1_out, xor_2_out, xor_3_out, xor_4_out,
       xor_5_out;

  and and_1 (and_1_out, B0, A0);
  // _4_to_1_MUX__x2___74153 #(.Facing("east")) 4_to_1_mux_x2_74153_1: pin names not known; wires that end beside it: B0, 1'b0, B1, B0, A0, 1'b0, 1'b0, n4_to_1_mux_x2_74153_1_p8, n4_to_1_mux_x2_74153_1_p9
  xor xor_1 (xor_1_out, A1, B1);
  xor xor_2 (xor_2_out, A0, B0);
  nor nor_1 (nor_1_out, A1, B1);
  nor nor_2 (nor_2_out, A0, B0);
  xor xor_3 (xor_3_out, A1, B1);
  xor xor_4 (xor_4_out, A0, B0);
  xor xor_5 (xor_5_out, xor_1_out, and_1_out);
  // _4_to_1_MUX__x2___74153 #(.Facing("east")) 4_to_1_mux_x2_74153_2: pin names not known; wires that end beside it: xor_2_out, n4_to_1_mux_x2_74153_1_p8, xor_4_out, nor_2_out, xor_5_out, n4_to_1_mux_x2_74153_1_p9, xor_3_out, nor_1_out, O1, 1'b0, O2, n4_to_1_mux_x2_74153_2_p12, n4_to_1_mux_x2_74153_2_p13
  // _3_to_8_decoder__74138 #(.Facing("east")) 3_to_8_decoder_74138_1: pin names not known; wires that end beside it: n4_to_1_mux_x2_74153_2_p12, n4_to_1_mux_x2_74153_2_p13, 1'b0, 1'b1, 1'b0, L0, L1, L2, L3, L1, L3
endmodule
